# Fritzing sketch ciclop_pcb (saved by Fritzing 0.9.2b)
circuit board: 6.88566cm x 5.36311cm
breadboards: 1

parts:
  MD09B1 = A4988 Stepper Motor Driver Carrier
  J5 = female pin header, 4 pins [form="♀ (female)"]
  J9 = female pin header, 2 pins [form="♀ (female)"]
  J8 = female pin header, 2 pins [form="♀ (female)"]
  Q2 = MOSFET-NCHANNEL [package=to220v]
  C1 = Capacitor Polarized [package=cpol-radial-100uf-25v]
  R1 = Resistor [tolerance=±5% resistance=220 package=THT]
  J1 = screw terminal, 2 pins
  Q1 = MOSFET-NCHANNEL [package=to220v]
  Nano1 = Arduino Nano v2.3

nets:
  N1: MD09B1.Enable, R1.Pin_0, Nano1.D9
  VDD: MD09B1.MS1, MD09B1.MS2, MD09B1.MS3, MD09B1.VDD, J9.pin2, J8.pin1, R1.Pin_1, Nano1.+5V
  N2: MD09B1.RESET, MD09B1.SLEEP
  N3: MD09B1.STEP, Nano1.D12
  N4: MD09B1.DIR, Nano1.D13
  N5: MD09B1.VMOT, C1.-, J1.pin2, Nano1.VIN
  N6: MD09B1.GROUND, Q2.S, C1.+, J1.pin1, Q1.S, Nano1.GND
  N7: MD09B1.OUT_2B, J5.pin4
  N8: MD09B1.OUT_2A, J5.pin3
  N9: MD09B1.OUT_1A, J5.pin2
  N10: MD09B1.OUT_1B, J5.pin1
  N11: J9.pin1, Q2.D
  N12: J8.pin2, Q1.D
  N13: Q2.G, Nano1.D2
  N14: Q1.G, Nano1.D3
